// Logisim project adder-1.circ as structural Verilog
module Adder_Sub_4 (
  input  D,
  input  [3:0] A,
  input  [3:0] B,
  input  [2:0] in_4,
  output OVERFLOW,
  output OVERFLOW_2,
  output [3:0] out_7
);

  wire codificador_1_s0, codificador_1_s1, codificador_1_s2, codificador_1_s3, codificador_1_s4,
       codificador_1_s5, not_1_out;
  wire [3:0] adder_4_1_out_4, buffer_right_1_s, or_gate_1_out_3, rot_l_1_abcd_2, rot_r_1_abcd_2,
       sub_4_1_out_4;

  Codificador codificador_1 (
    .S0(codificador_1_s0), .S1(codificador_1_s1), .S2(codificador_1_s2), .S3(codificador_1_s3),
    .S4(codificador_1_s4), .S5(codificador_1_s5), .in_1(in_4));  // open: S6, S7
  Buffer buffer_1 (.B(B), .Controle(codificador_1_s0), .S(out_7));
  adder_4 adder_4_1 (.OVERFLOW(OVERFLOW), .out_4(adder_4_1_out_4), .in_2(B), .in_1(A));
  Buffer buffer_2 (.B(adder_4_1_out_4), .Controle(codificador_1_s1), .S(out_7));
  Sub_4 sub_4_1 (.in_1(A), .out_3(OVERFLOW_2), .in_2(B), .out_4(sub_4_1_out_4));
  Buffer buffer_3 (.B(sub_4_1_out_4), .Controle(codificador_1_s2), .S(out_7));
  OR_gate or_gate_1 (.in_1(A), .in_2(B), .out_3(or_gate_1_out_3));
  Buffer buffer_4 (.B(or_gate_1_out_3), .Controle(codificador_1_s3), .S(out_7));
  Buffer_Inversor buffer_inversor_1 (.B(B), .Controle(codificador_1_s4), .S(out_7));
  rot_L rot_l_1 (.ABCD(A), .abcd_2(rot_l_1_abcd_2), .XY(B[1:0]));
  rot_R rot_r_1 (.ABCD(A), .abcd_2(rot_r_1_abcd_2), .XY(B[1:0]));
  Buffer__right buffer_right_1 (.B(rot_r_1_abcd_2), .Controle(not_1_out), .S(buffer_right_1_s));
  Buffer__right buffer_right_2 (.B(rot_l_1_abcd_2), .Controle(D), .S(buffer_right_1_s));
  not not_1 (not_1_out, D);
  Buffer buffer_5 (.B(buffer_right_1_s), .Controle(codificador_1_s5), .S(out_7));
endmodule

module Buffer (
  input  [3:0] B,
  input  Controle,
  output [3:0] S
);

  assign S[1] = Controle ? B[1] : 1'bz;  // Controlled_Buffer controlled_buffer_1
  assign S[3] = Controle ? B[3] : 1'bz;  // Controlled_Buffer controlled_buffer_2
  assign S[2] = Controle ? B[2] : 1'bz;  // Controlled_Buffer controlled_buffer_3
  assign S[0] = Controle ? B[0] : 1'bz;  // Controlled_Buffer controlled_buffer_4
endmodule

module Buffer__right (
  input  [3:0] B,
  input  Controle,
  output [3:0] S
);

  assign S[2] = Controle ? B[2] : 1'bz;  // Controlled_Buffer controlled_buffer_1
  assign S[3] = Controle ? B[3] : 1'bz;  // Controlled_Buffer controlled_buffer_2
  assign S[1] = Controle ? B[1] : 1'bz;  // Controlled_Buffer controlled_buffer_3
  assign S[0] = Controle ? B[0] : 1'bz;  // Controlled_Buffer controlled_buffer_4

  // Notes on the sheet:
  //   (FIz por motivos estéticos apenas)
  //   Idêntico ao buffer normal, mas com a porta de controle do lado direito.
endmodule

module Buffer_Inversor (
  input  [3:0] B,
  input  Controle,
  output [3:0] S
);

  assign S[3] = Controle ? ~B[3] : 1'bz;  // Controlled_Inverter controlled_inverter_1
  assign S[2] = Controle ? ~B[2] : 1'bz;  // Controlled_Inverter controlled_inverter_2
  assign S[1] = Controle ? ~B[1] : 1'bz;  // Controlled_Inverter controlled_inverter_3
  assign S[0] = Controle ? ~B[0] : 1'bz;  // Controlled_Inverter controlled_inverter_4
endmodule

module Codificador (
  input  [2:0] in_1,
  output S0,
  output S1,
  output S2,
  output S3,
  output S4,
  output S5,
  output S6,
  output S7
);

  wire not_1_out, not_2_out, not_3_out, not_4_out, not_5_out, not_6_out, not_7_out, not_8_out, not_9_out,
       not_10_out, not_11_out, not_12_out;

  not not_1 (not_1_out, in_1[2]);
  not not_2 (not_2_out, in_1[1]);
  not not_3 (not_3_out, in_1[0]);
  not not_4 (not_4_out, in_1[2]);
  not not_5 (not_5_out, in_1[1]);
  not not_6 (not_6_out, in_1[2]);
  not not_7 (not_7_out, in_1[0]);
  not not_8 (not_8_out, in_1[2]);
  not not_9 (not_9_out, in_1[1]);
  not not_10 (not_10_out, in_1[0]);
  not not_11 (not_11_out, in_1[1]);
  not not_12 (not_12_out, in_1[0]);
  and and_1 (S7, in_1[2], in_1[1], in_1[0]);
  and and_2 (S0, not_1_out, not_2_out, not_3_out);
  and and_3 (S1, not_4_out, not_5_out, in_1[0]);
  and and_4 (S2, not_6_out, in_1[1], not_7_out);
  and and_5 (S3, not_8_out, in_1[1], in_1[0]);
  and and_6 (S4, in_1[2], not_9_out, not_10_out);
  and and_7 (S5, in_1[2], not_11_out, in_1[0]);
  and and_8 (S6, in_1[2], in_1[1], not_12_out);
endmodule

module adder_4 (
  input  [3:0] in_1,
  input  [3:0] in_2,
  output OVERFLOW,
  output [3:0] out_4
);

  wire adder_1_2_c_out, adder_1_3_c_out, adder_1_4_c_out;

  Adder_1 adder_1_1 (.A(in_2[3]), .B(in_1[3]), .C_in(adder_1_2_c_out), .S(out_4[3]), .C_out(OVERFLOW));
  Adder_1 adder_1_2 (.A(in_2[2]), .B(in_1[2]), .C_in(adder_1_3_c_out), .S(out_4[2]), .C_out(adder_1_2_c_out));
  Adder_1 adder_1_3 (.A(in_2[1]), .B(in_1[1]), .C_in(adder_1_4_c_out), .S(out_4[1]), .C_out(adder_1_3_c_out));
  Adder_1 adder_1_4 (.A(in_2[0]), .B(in_1[0]), .C_in(1'b0), .S(out_4[0]), .C_out(adder_1_4_c_out));
endmodule

module Adder_1 (
  input  A,
  input  B,
  input  C_in,
  output S,
  output C_out
);

  wire and_1_out, and_2_out, xor_1_out;

  xor xor_1 (xor_1_out, A, B);
  and and_1 (and_1_out, B, A);
  and and_2 (and_2_out, C_in, xor_1_out);
  xor xor_2 (S, xor_1_out, C_in);
  or or_1 (C_out, and_2_out, and_1_out);
endmodule

module Sub_4 (
  input  [3:0] in_1,
  input  [3:0] in_2,
  output out_3,
  output [3:0] out_4
);

  wire sub_1_2_c_out, sub_1_3_c_out, sub_1_4_c_out;

  Sub_1 sub_1_1 (.A(in_1[3]), .B(in_2[3]), .S(out_4[3]), .C_in(sub_1_2_c_out), .C_out(out_3));
  Sub_1 sub_1_2 (.A(in_1[2]), .B(in_2[2]), .S(out_4[2]), .C_in(sub_1_3_c_out), .C_out(sub_1_2_c_out));
  Sub_1 sub_1_3 (.A(in_1[1]), .B(in_2[1]), .S(out_4[1]), .C_in(sub_1_4_c_out), .C_out(sub_1_3_c_out));
  Sub_1 sub_1_4 (.A(in_1[0]), .B(in_2[0]), .S(out_4[0]), .C_in(1'b0), .C_out(sub_1_4_c_out));
endmodule

module Sub_1 (
  input  A,
  input  B,
  input  C_in,
  output S,
  output C_out
);

  wire and_1_out, and_2_out, not_1_out, not_2_out, xor_1_out;

  not not_1 (not_1_out, A);
  xor xor_1 (xor_1_out, A, B);
  not not_2 (not_2_out, xor_1_out);
  and and_1 (and_1_out, B, not_1_out);
  and and_2 (and_2_out, C_in, not_2_out);
  xor xor_2 (S, xor_1_out, C_in);
  or or_1 (C_out, and_2_out, and_1_out);
endmodule

module rot_L (
  input  [1:0] XY,
  input  [3:0] ABCD,
  output [3:0] abcd_2
);

  wire and_1_out, and_2_out, and_3_out, and_4_out, and_5_out, and_6_out, and_7_out, and_8_out, and_9_out;

  and and_1 (and_1_out, ~XY[1], ~XY[0], ABCD[3]);  // AND_Gate
  and and_2 (and_2_out, ~XY[1], XY[0], ABCD[2]);  // AND_Gate
  and and_3 (and_3_out, XY[1], ~XY[0], ABCD[1]);  // AND_Gate
  and and_4 (and_4_out, XY[1], XY[0], ABCD[0]);
  and and_5 (and_5_out, ~XY[1], ~XY[0], ABCD[2]);  // AND_Gate
  and and_6 (and_6_out, ~XY[1], XY[0], ABCD[1]);  // AND_Gate
  and and_7 (and_7_out, XY[1], ~XY[0], ABCD[0]);  // AND_Gate
  and and_8 (and_8_out, ~XY[1], ~XY[0], ABCD[1]);  // AND_Gate
  and and_9 (and_9_out, ~XY[1], XY[0], ABCD[0]);  // AND_Gate
  and and_10 (abcd_2[0], ~XY[1], ~XY[0], ABCD[0]);  // AND_Gate
  or or_1 (abcd_2[3], and_1_out, and_2_out, and_3_out, and_4_out);
  or or_2 (abcd_2[2], and_5_out, and_6_out, and_7_out);
  or or_3 (abcd_2[1], and_8_out, and_9_out);
endmodule

module rot_R (
  input  [1:0] XY,
  input  [3:0] ABCD,
  output [3:0] abcd_2
);

  wire and_1_out, and_2_out, and_3_out, and_4_out, and_5_out, and_6_out, and_7_out, and_8_out, and_9_out;

  and and_1 (and_1_out, ~XY[1], ~XY[0], ABCD[0]);  // AND_Gate
  and and_2 (and_2_out, ~XY[1], XY[0], ABCD[1]);  // AND_Gate
  and and_3 (and_3_out, XY[1], ~XY[0], ABCD[2]);  // AND_Gate
  and and_4 (and_4_out, XY[1], XY[0], ABCD[3]);
  and and_5 (and_5_out, ~XY[1], ~XY[0], ABCD[1]);  // AND_Gate
  and and_6 (and_6_out, ~XY[1], XY[0], ABCD[2]);  // AND_Gate
  and and_7 (and_7_out, XY[1], ~XY[0], ABCD[3]);  // AND_Gate
  and and_8 (and_8_out, ~XY[1], ~XY[0], ABCD[2]);  // AND_Gate
  and and_9 (and_9_out, ~XY[1], XY[0], ABCD[3]);  // AND_Gate
  and and_10 (abcd_2[3], ~XY[1], ~XY[0], ABCD[3]);  // AND_Gate
  or or_1 (abcd_2[0], and_1_out, and_2_out, and_3_out, and_4_out);
  or or_2 (abcd_2[1], and_5_out, and_6_out, and_7_out);
  or or_3 (abcd_2[2], and_8_out, and_9_out);
endmodule

module OR_gate (
  input  [3:0] in_1,
  input  [3:0] in_2,
  output [3:0] out_3
);

  or or_1 (out_3[3], in_1[3], in_2[3]);
  or or_2 (out_3[2], in_1[2], in_2[2]);
  or or_3 (out_3[1], in_1[1], in_2[1]);
  or or_4 (out_3[0], in_1[0], in_2[0]);
endmodule
